# Fritzing sketch Diagram (saved by Fritzing 0.9.10b)

parts:
  Part1 = Arduino Uno (Rev3) - ICSP
  DHT1 = Humidity and Temperature Sensor DHT11
  Part2 = LCD1602-I2C
  A1 = 2 channel relay module [package=THT]
  A2 = 2 channel relay module [package=THT]
  Button_Module_1 = KY-004 Key Switch Module [package="Breakout board"]
  Button_Module_2 = KY-004 Key Switch Module [package="Breakout board"]

nets:
  N1: Part1.A4/SDA, Part2.SDA
  N2: Part1.A5/SCL, Part2.SCL
  VIN: Part1.5V, Part2.VCC, A1.pin_13, A2.pin_13, Button_Module_1.Vin, Button_Module_2.Vin
  N3: Part1.D8, Button_Module_2.S
  GND: Part1.GND, DHT1.GND_2, Part2.GND, A1.pin_14, A2.pin_14, Button_Module_1.-, Button_Module_2.-
  N4: Part1.D2, DHT1.Data-signal
  N5: Part1.D3_PWM, A2.pin_16
  N6: Part1.D4, A2.pin_15
  N7: Part1.D5_PWM, A1.pin_16
  N8: Part1.D6_PWM, A1.pin_15
  N9: Part1.D7, Button_Module_1.S
  3V3: Part1.3V3, DHT1.Vcc

custom parts:
  Humidity and Temperature Sensor DHT11: Digital relative humidity & temperature sensor DHT11
  LCD1602-I2C: A standard character display, usually with 2x16 characters. Comes in many colors with LCM1602 IIC attached.
  2 channel relay module: 2 channel Relay Module 5V 12V 24V High and Low Level Trigger Relay Control With Optocoupler Two Way relays DC 5 V 12 V 24 V Volt.
  KY-004 Key Switch Module: Arduino Key Switch Module Keyes KY-004 is a push button that will output a high signal when pressed.
